# Fritzing sketch Untitled Sketch (saved by Fritzing 0.9.3b)
breadboards: 1

parts:
  Част1 = Arduino Uno (Rev3)
  U1 = LCD-16X2 [package=lcd-16x2]  # not connected
  U2 = POT [package=pot_mammoth]
  R1 = PHOTOCELL [package=photocell-kit]
  R2 = Resistor [tolerance=±5% resistance=220 package=THT]
  U3 = RELAY [package=relay-jzc]

nets (from the breadboard view):
  N1: Част1.A0, R1.P$2, R2.Pin_0
  N2: Част1.D7, U3.MAIN
  N3: Част1.5V, U2.S, R1.P$1
  N4: Част1.GND, U2.E, U3.COIL1

// code stored in the sketch: Untitled.ino

#include <LiquidCrystal.h> //Load Liquid Crystal Library
LiquidCrystal LCD(11,10,9,2,3,4,5);  //Create Liquid Crystal Object called LCD

int lightPin = 0;  //pin for Photoresistor
int TranslateAnalog = 0;

void setup() 
{  
  pinMode (7, OUTPUT);
  LCD.begin(16,2); //Tell Arduino to start your 16 column 2 row LCD
}

void loop() {
  TranslateAnalog = analogRead(lightPin);
  if(TranslateAnalog>355) {
    LCD.clear();
    LCD.setCursor(0,0);  //Set LCD cursor to upper left corner, column 0, row 0
  LCD.print("ROOM LIGHT");  //Print Message on First Row
      digitalWrite(7, HIGH);
      LCD.setCursor(0,1);   //Set Cursor again to first column of second row     
      LCD.print("TURN OFF");  //Print your units.
      delay(5000); //TURN ON LIGHT AFTER 5000 MILISECONDS      
    }
    //If Photoreistor Value is below 355 it will turn LED ON
    if(TranslateAnalog<355) {
      LCD.clear();
      LCD.setCursor(0,0);  //Set LCD cursor to upper left corner, column 0, row 0
  LCD.print("ROOM LIGHT");  //Print Message on First Row
      digitalWrite(7, LOW);
      LCD.setCursor(0,1);   //Set Cursor again to first column of second row
      LCD.print("TURN ON");  //Print your units.
      delay(5000);//TURN OFF LIGHT AFTER 5000 MILISECONDS      
    }
   
  }
